// Logisim project TLB_Design.circ as structural Verilog: 3 circuits, main circuit main
module main (
  input  [4:0] PageNumberIn,
  input  [4:0] FrameNumberIn,
  input  WriteEnabled,
  output [4:0] FrameNumberOut,
  output Found
);

  CacheLines cachelines_1 (
    .Tag(PageNumberIn[4:2]), .Index(PageNumberIn[1:0]), .FrameNumberIn(FrameNumberIn),
    .WriteEnabled(WriteEnabled), .Found(Found), .FrameNumberOut(FrameNumberOut));
endmodule

module Cacheline (
  input  [2:0] TagIn,
  input  [4:0] DataIn,
  input  WriteEnabled,
  output [2:0] TagOut,
  output [4:0] FrameNumberOut,
  output IsInitializedOut
);

  Register #(.width(3)) TagStore (.D(TagIn), .en(WriteEnabled), .clk(WriteEnabled), .Q(TagOut));  // open: clr
  Register #(.width(5)) FrameNumberStore (
    .D(DataIn), .en(WriteEnabled), .clk(WriteEnabled), .Q(FrameNumberOut));  // open: clr
  D_Flip_Flop d_ff_1 (.D(1'b1), .clk(WriteEnabled), .Q(IsInitializedOut));  // open: Qn, preset, reset
endmodule

module CacheLines (
  input  [2:0] Tag,
  input  [1:0] Index,
  input  [4:0] FrameNumberIn,
  input  WriteEnabled,
  output Found,
  output [4:0] FrameNumberOut
);

  wire and_1_out, and_2_out, and_3_out, and_4_out, comparator_1_eq, decoder_1_out0, decoder_1_out1,
       decoder_1_out2, decoder_1_out3;
  wire [2:0] cacheline_1_tagout, cacheline_2_tagout, cacheline_3_tagout, cacheline_4_tagout,
       multiplexer_1_out;
  wire [4:0] cacheline_1_framenumberout, cacheline_2_framenumberout, cacheline_3_framenumberout,
       cacheline_4_framenumberout;
  wire [8:8] cacheline_1_isinitializedout, cacheline_2_isinitializedout, cacheline_3_isinitializedout,
       cacheline_4_isinitializedout, multiplexer_1_out_2;

  Decoder #(.select(2)) decoder_1 (
    .out0(decoder_1_out0), .out1(decoder_1_out1), .out2(decoder_1_out2), .out3(decoder_1_out3), .sel(Index));  // open: en
  and and_1 (and_1_out, decoder_1_out0, WriteEnabled);
  and and_2 (and_2_out, decoder_1_out1, WriteEnabled);
  and and_3 (and_3_out, decoder_1_out2, WriteEnabled);
  and and_4 (and_4_out, decoder_1_out3, WriteEnabled);
  Comparator #(.width(3)) comparator_1 (.a(multiplexer_1_out), .b(Tag), .eq(comparator_1_eq));  // open: gt, lt
  and and_5 (Found, comparator_1_eq, multiplexer_1_out_2[8]);
  Cacheline cacheline_1 (
    .TagIn(Tag), .DataIn(FrameNumberIn), .WriteEnabled(and_1_out), .TagOut(cacheline_1_tagout),
    .FrameNumberOut(cacheline_1_framenumberout), .IsInitializedOut(cacheline_1_isinitializedout[8]));
  Cacheline cacheline_2 (
    .TagIn(Tag), .DataIn(FrameNumberIn), .WriteEnabled(and_2_out), .TagOut(cacheline_2_tagout),
    .FrameNumberOut(cacheline_2_framenumberout), .IsInitializedOut(cacheline_2_isinitializedout[8]));
  Cacheline cacheline_3 (
    .TagIn(Tag), .DataIn(FrameNumberIn), .WriteEnabled(and_3_out), .TagOut(cacheline_3_tagout),
    .FrameNumberOut(cacheline_3_framenumberout), .IsInitializedOut(cacheline_3_isinitializedout[8]));
  Cacheline cacheline_4 (
    .TagIn(Tag), .DataIn(FrameNumberIn), .WriteEnabled(and_4_out), .TagOut(cacheline_4_tagout),
    .FrameNumberOut(cacheline_4_framenumberout), .IsInitializedOut(cacheline_4_isinitializedout[8]));
  Multiplexer #(.select(2), .width(9)) multiplexer_1 (
    .in0({cacheline_1_isinitializedout[8], cacheline_1_framenumberout, cacheline_1_tagout}),
    .in1({cacheline_2_isinitializedout[8], cacheline_2_framenumberout, cacheline_2_tagout}),
    .in2({cacheline_3_isinitializedout[8], cacheline_3_framenumberout, cacheline_3_tagout}),
    .in3({cacheline_4_isinitializedout[8], cacheline_4_framenumberout, cacheline_4_tagout}),
    .out({multiplexer_1_out_2[8], FrameNumberOut, multiplexer_1_out}), .sel(Index));
endmodule
